# Fritzing sketch 2 (saved by Fritzing 0.9.4)
breadboards: 1

parts:
  VCC1 = 4 x AAA Battery Mount
  R1 = Resistor [tolerance=±5% resistance=220 package="0402 [SMD]"]
  LED1 = LED - 3mm [color="Red (633nm)" package="3 mm [THT]"]
  U1 = 74HC04_HEX_INVERTER [package=dil14]

nets:
  N1: VCC1.-, LED1.cathode, U1.GND
  N2: VCC1.+, R1.Pin_0, U1.VCC
  N3: R1.Pin_1, U1.1A
  N4: LED1.anode, U1.6Y
  N5: U1.1Y, U1.2A
  N6: U1.2Y, U1.3A
  N7: U1.3Y, U1.4A
  N8: U1.4Y, U1.5A
  N9: U1.5Y, U1.6A
