// Logisim project 1.circ as structural Verilog: 1 circuit, main circuit main
module main (
  input  A0,
  input  B,
  input  C_in,
  output S,
  output C_out
);

  wire and_1_out, and_2_out, xor_1_out;

  xor xor_1 (xor_1_out, B, A0);
  and and_1 (and_1_out, B, A0);
  xor xor_2 (S, C_in, xor_1_out);
  and and_2 (and_2_out, C_in, xor_1_out);
  or or_1 (C_out, and_2_out, and_1_out);
endmodule
