// Logisim project 2.circ as structural Verilog: 1 circuit, main circuit main
module main (
  input  A0,
  input  B0,
  input  C_in,
  input  A1,
  input  B1,
  input  A2,
  input  B2,
  input  A3,
  input  B3,
  output S0,
  output C_out0,
  output S1,
  output C_out1,
  output S2,
  output C_out2,
  output V,
  output S3,
  output C_out3
);

  wire and_1_out, and_2_out, and_3_out, and_4_out, and_5_out, and_6_out, and_7_out, and_8_out, xor_1_out,
       xor_2_out, xor_3_out, xor_4_out, xor_5_out, xor_6_out, xor_7_out, xor_8_out;

  xor xor_1 (xor_1_out, B0, C_in);
  xor xor_2 (xor_2_out, B1, C_in);
  xor xor_3 (xor_3_out, B2, C_in);
  xor xor_4 (xor_4_out, B3, C_in);
  xor xor_5 (xor_5_out, xor_1_out, A0);
  and and_1 (and_1_out, xor_1_out, A0);
  xor xor_6 (xor_6_out, xor_2_out, A1);
  and and_2 (and_2_out, xor_2_out, A1);
  xor xor_7 (xor_7_out, xor_3_out, A2);
  and and_3 (and_3_out, xor_3_out, A2);
  xor xor_8 (xor_8_out, xor_4_out, A3);
  and and_4 (and_4_out, xor_4_out, A3);
  xor xor_9 (S0, C_in, xor_5_out);
  and and_5 (and_5_out, C_in, xor_5_out);
  xor xor_10 (S1, C_out0, xor_6_out);
  and and_6 (and_6_out, C_out0, xor_6_out);
  xor xor_11 (S2, C_out1, xor_7_out);
  and and_7 (and_7_out, C_out1, xor_7_out);
  xor xor_12 (S3, C_out2, xor_8_out);
  and and_8 (and_8_out, C_out2, xor_8_out);
  or or_1 (C_out0, and_5_out, and_1_out);
  or or_2 (C_out1, and_6_out, and_2_out);
  or or_3 (C_out2, and_7_out, and_3_out);
  or or_4 (C_out3, and_8_out, and_4_out);
  xor xor_13 (V, C_out2, C_out3);
endmodule
